# Fritzing sketch i2cencoders (saved by Fritzing 0.9.3b)
circuit board: 6.5cm x 4cm
breadboards: 1

parts:
  J1 = female pin header, 2 pins [form="♀ (female)"]
  J2 = female pin header, 2 pins [form="♀ (female)"]
  J3 = female pin header, 2 pins [form="♀ (female)"]
  J4 = female pin header, 22 pins [form="♀ (female)"]
  J5 = female pin header, 1 pin [form="♀ (female)"]
  Part1 = Arduino Pro Mini (3.3V)
  J6 = female pin header, 4 pins [form="♀ (female)"]
  J7 = female pin header, 1 pin [form="♀ (female)"]
  J8 = female pin header, 1 pin [form="♀ (female)"]
  J9 = female pin header, 1 pin [form="♀ (female)"]
  J10 = female pin header, 1 pin [form="♀ (female)"]

nets:
  N1: J1.pin1, J4.pin5
  N2: J1.pin2, J4.pin4
  N3: J2.pin1, J4.pin13
  N4: J2.pin2, J4.pin12
  N5: J3.pin1, J4.pin20, J7.pin1
  N6: J3.pin2, J4.pin19
  N7: J4.pin1, Part1.TXO
  N8: J4.pin2, Part1.D2
  N9: J4.pin3, Part1.D3
  N10: J4.pin9, Part1.D4
  N11: J4.pin10, Part1.D5
  N12: J4.pin11, Part1.D6
  N13: J4.pin16, Part1.D7
  N14: J4.pin17, Part1.D8
  N15: J4.pin18, Part1.D9
  N16: J5.pin1, Part1.VCC
  N17: Part1.A4, J6.pin2
  N18: Part1.A5, J6.pin1
  N19: Part1.RAW, J6.pin3
  N20: Part1.GND, J9.pin1
  N21: J6.pin4, J8.pin1, J10.pin1

notes:
  buczek.cc
